// Logisim project E21CSEU0245_ques1.circ as structural Verilog: 1 circuit, main circuit main
module main (
  input  I0,
  input  I1,
  input  I2,
  input  I3,
  input  S0,
  input  S1,
  output out_7
);

  wire and_1_out, and_2_out, and_3_out, and_4_out, not_1_out, not_2_out;

  not not_1 (not_1_out, S0);
  not not_2 (not_2_out, S1);
  and and_1 (and_1_out, I0, not_2_out, not_1_out);
  and and_2 (and_2_out, I1, not_2_out, S0);
  and and_3 (and_3_out, I2, S1, S1);
  and and_4 (and_4_out, I3, S1, S0);
  or or_1 (out_7, and_1_out, and_2_out, and_3_out, and_4_out);

  // Notes on the sheet:
  //   Ayushman Pranav E212CSEU0245
  //   4:1 mux MULTIPLEXER
endmodule
