// Logisim project E21CSEU0245_ques2.circ as structural Verilog: 1 circuit, main circuit main
module main (
  input  A,
  input  B,
  input  C,
  output Sum,
  output Carry
);

  wire and_1_out, and_2_out, xor_1_out;

  xor xor_1 (xor_1_out, A, B);
  and and_1 (and_1_out, A, B);
  xor xor_2 (Sum, xor_1_out, C);
  and and_2 (and_2_out, C, xor_1_out);
  or or_1 (Carry, and_2_out, and_1_out);

  // Notes on the sheet:
  //   Ayushman Pranav E21CSEU0245
  //   FULL ADDER
endmodule
