// Logisim project E21CSEU0245_ques3.circ as structural Verilog: 1 circuit, main circuit sr flip flop
module sr_flip_flop (
  input  in_1,
  input  in_2,
  input  in_3,
  output out_4
);

  wire and_1_out, and_2_out, not_1_out, not_2_out, s_r_ff_1_q, undriven;

  not not_1 (not_1_out, in_2);
  and and_1 (and_1_out, in_2, in_3);
  and and_2 (and_2_out, not_1_out, in_3, in_1);
  S_R_Flip_Flop s_r_ff_1 (.S(and_1_out), .clk(undriven), .R(and_2_out), .Q(s_r_ff_1_q));  // open: Qn, preset, reset, en
  not not_2 (not_2_out, in_3);
  and and_3 (out_4, in_1, s_r_ff_1_q, not_2_out);

  // Notes on the sheet:
  //   Ayushman Pranav E21CSEU0245
endmodule
