// Logisim project E21CSEU0245_Lab2_Q1.circ as structural Verilog: 1 circuit, main circuit main
module main (
  input  in_1,
  input  in_2,
  output out_3
);

  wire clock_1_out, d_ff_1_q, multiplexer_1_out, not_1_out;

  not not_1 (not_1_out, in_2);
  Multiplexer multiplexer_1 (.in0(in_1), .in1(not_1_out), .out(multiplexer_1_out), .sel(d_ff_1_q));  // open: en
  D_Flip_Flop d_ff_1 (.clk(clock_1_out), .D(multiplexer_1_out), .Q(d_ff_1_q), .Qn(out_3));  // open: preset, en, reset
  Clock clock_1 (.out(clock_1_out));

  // Notes on the sheet:
  //   AYUSHMAN PRANAV
  //   E21CSEU0245
  //   2*1 MUX
  //   D FLIP FLOP
  //   JK FLIP FLOP
endmodule
