// Logisim project E21CSEU0245_Lab2_Q3.circ as structural Verilog: 2 circuits, main circuit main
module main (
  input  in_1,
  input  in_2,
  input  in_3,
  input  in_4,
  output out_5,
  output out_6
);

  wire not_1_out;

  not not_1 (not_1_out, in_1);
  _4x1mux u_4x1mux_1 (
    .in_1(in_1), .in_2(not_1_out), .in_3(not_1_out), .in_4(in_1), .in_5(in_3), .in_6(in_4), .out_7(out_5));
  _4x1mux u_4x1mux_2 (.in_1(in_2), .in_2(in_2), .in_3(in_2), .in_4(in_2), .in_5(in_3), .in_6(in_4), .out_7(out_6));
endmodule

module _4x1mux (
  input  in_1,
  input  in_2,
  input  in_3,
  input  in_4,
  input  in_5,
  input  in_6,
  output out_7
);

  wire and_1_out, and_2_out, and_3_out, and_4_out, not_1_out, not_2_out;

  not not_1 (not_1_out, in_5);
  not not_2 (not_2_out, in_6);
  and and_1 (and_1_out, in_1, not_1_out, not_2_out);
  and and_2 (and_2_out, in_2, not_1_out, in_6);
  and and_3 (and_3_out, in_3, in_5, not_2_out);
  and and_4 (and_4_out, in_4, in_5, in_6);
  or or_1 (out_7, and_1_out, and_2_out, and_3_out, and_4_out);
endmodule
