// Logisim project E21CSEU0245_Lab2_Q4.circ as structural Verilog: 4 circuits, main circuit E21CSEU0075_Lab2_Q4
module main (
  input  J,
  input  K,
  output Q
);

  wire clock_1_out, multiplexer_1_out, not_1_out;

  Multiplexer multiplexer_1 (.in0(J), .in1(not_1_out), .out(multiplexer_1_out), .sel(Q));  // open: en
  not not_1 (not_1_out, K);
  Clock clock_1 (.out(clock_1_out));
  D_Flip_Flop d_ff_1 (.clk(clock_1_out), .D(multiplexer_1_out), .Q(Q));  // open: Qn, preset, en, reset

  // Notes on the sheet:
  //   S
  //   Raghavendra Prasad_E21CSEU0075
  //   D
endmodule

module E21CSEU0075_Lab2_Q2 (
  input  A,
  input  B,
  input  C,
  input  D,
  output Y
);

  wire and_1_out, and_2_out, not_1_out, not_2_out;

  not not_1 (not_1_out, C);
  not not_2 (not_2_out, D);
  and and_1 (and_1_out, A, B, not_1_out);
  and and_2 (and_2_out, B, not_2_out);
  or or_1 (Y, and_1_out, and_2_out, C);

  // Notes on the sheet:
  //   E21CSEU0075_Raghavendra Prasad
endmodule

module E21CSEU0075_Lab2_Q3 (
  input  A,
  input  B,
  input  Bin,
  output Difference,
  output Borrow
);

  wire and_1_out, and_2_out, not_1_out, not_2_out, xor_1_out;

  not not_1 (not_1_out, A);
  xor xor_1 (xor_1_out, A, B);
  and and_1 (and_1_out, B, not_1_out);
  xor xor_2 (Difference, xor_1_out, Bin);
  not not_2 (not_2_out, xor_1_out);
  and and_2 (and_2_out, Bin, not_2_out);
  or or_1 (Borrow, and_2_out, and_1_out);

  // Notes on the sheet:
  //   E21CSEU0075_Raghavendra Prasad
endmodule

module E21CSEU0075_Lab2_Q4 (
  input  [3:0] in_1,
  input  [3:0] in_2,
  input  in_3,
  output [3:0] out_4,
  output [3:0] out_5,
  output [3:0] out_6,
  output out_7
);

  wire adder_1_cout, adder_2_cout, adder_3_cout;

  Adder #(.width(1)) adder_1 (.a(in_1[0]), .b(in_2[0]), .out(out_6[0]), .cin(in_3), .cout(adder_1_cout));
  Adder #(.width(1)) adder_2 (.a(in_1[1]), .b(in_2[1]), .out(out_6[1]), .cin(adder_1_cout), .cout(adder_2_cout));
  Adder #(.width(1)) adder_3 (.a(in_1[2]), .b(in_2[2]), .out(out_6[2]), .cin(adder_2_cout), .cout(adder_3_cout));
  Adder #(.width(1)) adder_4 (.a(in_1[3]), .b(in_2[3]), .out(out_6[3]), .cin(adder_3_cout), .cout(out_7));
  and and_1 (out_4[0], in_1[0], in_2[0]);
  and and_2 (out_4[1], in_1[1], in_2[1]);
  and and_3 (out_4[2], in_1[2], in_1[2], in_2[2]);
  and and_4 (out_4[3], in_1[3], in_2[3]);
  or or_1 (out_5[0], in_1[0], in_2[0]);
  or or_2 (out_5[1], in_1[1], in_2[1]);
  or or_3 (out_5[2], in_1[2], in_2[2]);
  or or_4 (out_5[3], in_1[3], in_2[3]);
endmodule
