// Logisim project E21CSEU0245_Lab2_Q5.circ as structural Verilog: 1 circuit, main circuit main
module main (
  input  I2,
  input  I4,
  input  I6,
  input  I1,
  input  I3,
  input  I5,
  input  I7,
  output out_8,
  output out_9,
  output out_10
);

  or or_1 (out_8, I7, I6, I5, I4);
  or or_2 (out_9, I7, I6, I3, I2);
  or or_3 (out_10, I7, I5, I3, I1);
endmodule
